# Fritzing sketch raindrops (saved by Fritzing 0.8.7b)

parts:
  YL-83_-_Control_Board1 = YL-83 Rain Sensor - Control Board
  YL-83_-_Detection_Board1 = YL-83 Rain Sensor - Detection Board
  Part1 = Arduino Uno (Rev3)

nets:
  VCC: YL-83_-_Control_Board1.VCC, Part1.5V
  GND: YL-83_-_Control_Board1.GND, Part1.GND
  N1: YL-83_-_Control_Board1.DO, Part1.D7
  N2: YL-83_-_Control_Board1.POS, YL-83_-_Detection_Board1.POS
  N3: YL-83_-_Control_Board1.NEG, YL-83_-_Detection_Board1.NEG

custom parts:
  YL-83 Rain Sensor - Control Board: The YL-83 is a rain sensor that has more resistance when dry and less resistance when wet. The module runs at 5V.
  YL-83 Rain Sensor - Detection Board: The YL-83 is a rain sensor that has more resistance when dry and less resistance when wet. The module runs at 5V.
